# Fritzing sketch Schematics (saved by Fritzing 0.9.0b)
breadboards: 1

parts:
  Part1 = Arduino Uno (Rev3)
  R5 = Resistor [tolerance=±5% resistance=1k package=THT]
  R1 = Photocell (LDR) [package=THT]
  R2 = Resistor [tolerance=±5% resistance=10k package=THT]
  Part2 = Humidity Sensor - HIH-4030 Breakout
  R6 = Resistor [tolerance=±5% resistance=33 package=THT]
  R4 = Resistor [tolerance=±5% resistance=1k package=THT]
  LCD1 = LCD screen

nets:
  N1: Part1.A0, R2.Pin_1, Part2.OUT
  N2: Part1.A1, R5.Pin_1, R1.pin_0
  N3: Part1.D12/MISO, LCD1.RS
  GND: Part1.GND, R5.Pin_0, Part2.GND, R6.Pin_0, R4.Pin_0, LCD1.VSS, LCD1.R/W, LCD1.E
  N4: Part1.D2, LCD1.DB4
  N5: Part1.D3_PWM, LCD1.DB5
  N6: Part1.D4, LCD1.DB6
  N7: Part1.D5_PWM, LCD1.DB7
  5V: Part1.5V, R1.pin_1, LCD1.VDD, LCD1.LED+
  N8: R2.Pin_0, Part2.VCC
  N9: R6.Pin_1, LCD1.LED-
  N10: R4.Pin_1, LCD1.V0

notes:
  light sensor
  moisture sensor
  Pin 16
  Pin 1
  LCD 20x4
